# Fritzing sketch buttonBoard (saved by Fritzing 0.9.4)

parts:
  U2 = LuaNode32 / ESP32
  LED1 = RGB LED - (4 legs) [package="5 mm [THT]"]
  S1 = Pushbutton [package="[THT]"]
  R1 = Resistor [tolerance=±5% resistance=220 package="0805 [SMD]"]

nets:
  N1: U2.D25, LED1.red_cathode
  N2: U2.D26, LED1.green_cathode
  N3: U2.D27, LED1.blue_cathode
  N4: U2.GND, LED1.common_anode, S1.Pin_1, S1.Pin_2, R1.Pin_1
  N5: U2.3V3, S1.Pin_3, S1.Pin_4
  N6: U2.D4, R1.Pin_0

custom parts:
  LuaNode32 / ESP32: ESP32 based LuaNode32
