# Fritzing sketch doorBoard (saved by Fritzing 0.9.4)

parts:
  U1 = LuaNode32 / ESP32
  J1 = Basic Servo
  PIR2 = PIR sensor

nets:
  GND: U1.GND, J1.gnd, PIR2.GND
  VIN: U1.Vin, J1.vcc, PIR2.VDD
  N1: U1.D4, PIR2.SIG
  N2: U1.D19, J1.pulse

custom parts:
  LuaNode32 / ESP32: ESP32 based LuaNode32
